// Digital circuit Ejercicio2-UO281827.dig as structural Verilog
module Ejercicio2_UO281827 (
  input  e_2,
  input  e_1,
  input  e_0,
  output out_4
);

  wire mux2_1_p4, nand_1_out, not_1_out, xor_1_out;

  nand nand_1 (nand_1_out, e_2, e_1);
  xor xor_1 (xor_1_out, e_1, e_0);
  not not_1 (not_1_out, e_0);
  // mux2 mux2_1: pin names not known; wires that end beside it: nand_1_out, xor_1_out, not_1_out, mux2_1_p4
  and and_1 (out_4, mux2_1_p4, not_1_out);
endmodule
