// Digital circuit Ejercicio3 UO281827.dig as structural Verilog
module Ejercicio3_UO281827 (
  input  A_3,
  input  A_2,
  input  A_1,
  input  A_0,
  input  B_3,
  input  B_2,
  input  B_1,
  input  B_0,
  input  Op_1,
  input  Op_0,
  input  compl_1,
  input  cin,
  output S_3,
  output S_2,
  output S_1,
  output S_0,
  output ZF,
  output CF,
  output OF,
  output SF
);

  // alu4 alu4_1: pin names not known; wires that end beside it: Op_1, Op_0, compl_1, cin, A_3, A_2, S_3, A_1, S_2, A_0, S_1, B_3, S_0, B_2, B_1, B_0, ZF, CF, OF, SF
endmodule
