// Digital circuit Eje2_circuito2.dig as structural Verilog
module Eje2_circuito2 (
  input  e2,
  input  e1,
  input  e0,
  output s
);

  wire not_1_out, or_1_out;

  not not_1 (not_1_out, e1);
  or or_1 (or_1_out, e2, not_1_out);
  and and_1 (s, or_1_out, e0);
endmodule
