// Digital circuit EjercicioAdicional6.dig as structural Verilog
module EjercicioAdicional6 (
  input  A_n_1,
  input  B_n_1,
  input  S_n_1,
  output Ov,
  output Neil
);

  // gen_ov_s George_Bush: pin names not known; wires that end beside it: A_n_1, B_n_1, S_n_1, Ov
  and and_1 (Neil, S_n_1, Ov);
endmodule

/* Test case:
A_{n-1}	B_{n-1}	S_{n-1}	Ov	Neil
0	0	0	0	0
1	0	0	0	0
0	1	0	0	0
0	0	1	1	1
1	1	1	0	0
*/
