// Digital circuit reg4-tri.dig as structural Verilog
module reg4_tri (
  input  Read,
  input  Write,
  input  d0,
  input  d3,
  input  d2,
  input  d1
);

  wire d_ff_1_q, d_ff_2_q, d_ff_3_q, d_ff_4_q;

  D_FF d_ff_1 (.D(d3), .C(Write), .Q(d_ff_1_q));  // open: nQ
  assign d3 = Read ? d_ff_1_q : 1'bz;  // Driver driver_1
  D_FF d_ff_2 (.D(d2), .C(Write), .Q(d_ff_2_q));  // open: nQ
  assign d2 = Read ? d_ff_2_q : 1'bz;  // Driver driver_2
  D_FF d_ff_3 (.D(d1), .C(Write), .Q(d_ff_3_q));  // open: nQ
  assign d1 = Read ? d_ff_3_q : 1'bz;  // Driver driver_3
  D_FF d_ff_4 (.D(d0), .C(Write), .Q(d_ff_4_q));  // open: nQ
  assign d0 = Read ? d_ff_4_q : 1'bz;  // Driver driver_4
endmodule
